# Fritzing sketch Clock_Alarm (saved by Fritzing 1.0.5)
perfboards: 1

parts:
  A1 = Esp32-c3 super mini
  J1 = Piezo Speaker
  S1 = Pushbutton [package="[THT]"]
  S2 = Pushbutton [package="[THT]"]
  Деталь1 = GY-BMEP280 Barometric Pressure Sensor - Breakout
  TP1 = TP4056 [chip_label=TP4056 package="DIP (Dual Inline) [THT]"]
  LED1 = LED - 5mm [color="Red (633nm)" current=0.030A package="5 mm [THT]"]
  IC1 = Voltage Regulator [package=to-92]
  C1 = Electrolytic Capacitor [capacitance=1µF voltage=35V package="100 mil [THT, electrolytic]"]
  C2 = Ceramic Capacitor [capacitance=100nF voltage=35V package="100 mil [THT, multilayer]"]
  R1 = Resistor [tolerance=±5% power=0.25W resistance=10k package=THT]
  R2 = Resistor [tolerance=±5% power=0.25W resistance=10k package=THT]
  S4 = Toggle Switch [package=THT]
  R3 = Resistor [tolerance=±5% power=0.25W resistance=220 package=THT]
  BAT1 = LIPO-2000mAh [package=lipo-2000]
  R4 = Resistor [tolerance=±5% power=0.25W resistance=10k package=THT]
  R5 = Resistor [tolerance=±5% power=0.25W resistance=10k package=THT]
  R6 = Resistor [tolerance=±5% power=0.25W resistance=10k package=THT]
  S5 = Pushbutton [package="[THT]"]
  OLED1 = OLED 128x64 I2C Monochrome Display
  OLED2 = OLED 128x64 I2C Monochrome Display

nets:
  N1: A1.Pin_4, Деталь1.SDA, OLED1.SDA, OLED2.SDA
  N2: A1.Pin_6, Деталь1.SCL, OLED1.SCK, OLED2.SCK
  N3: A1.Pin_8, R3.Pin_1
  N4: A1.Pin_9, R4.Pin_1, S5.Pin_1, S5.Pin_2
  N5: A1.Pin_10, S2.Pin_1, S2.Pin_2, R5.Pin_1
  N6: A1.Pin_11, S1.Pin_1, S1.Pin_2, R6.Pin_1
  N7: A1.Pin_12, J1.pin2
  N8: A1.Pin_13, R1.Pin_1, R2.Pin_1
  N9: A1.Pin_14, S1.Pin_3, S1.Pin_4, S2.Pin_3, S2.Pin_4, S5.Pin_3, S5.Pin_4, OLED2.VDD
  GND: A1.Pin_15, J1.pin1, Деталь1.GND, TP1.pin6, LED1.cathode, IC1.GND, C1.+, C2.1, R1.Pin_0, R4.Pin_0, R5.Pin_0, R6.Pin_0, OLED1.GND, OLED2.GND
  VCC: Деталь1.VCC, R2.Pin_0, S4.L2, OLED1.VDD
  N10: TP1.pin3, IC1.IN
  N11: TP1.pin4, BAT1.+
  N12: TP1.pin5, BAT1.-
  N13: LED1.anode, R3.Pin_0
  N14: IC1.OUT, C1.-, C2.0, S4.COM

custom parts:
  Esp32-c3 super mini: ESP32-C3 Development Board ESP32 SuperMini Development Board ESP32 Development Board WiFi Bluetooth.
  GY-BMEP280 Barometric Pressure Sensor - Breakout: The BME280 is a chip which was originally designed for the next generation of smartphones. It is made up of a very accurate pressure sensor and an associated temperature sensor which helps calibrate the pressure readings. And just for fun they threw in a pretty solid humidity sensor in there as well! So with an I2C connection you have access to enough weather data to make some pretty good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
  TP4056: A DIP stand-in part for whatever IC you want. With 6 pins on a 300mil dual inline package (DIP) footprint.
